# Fritzing sketch L6203 (saved by Fritzing 0.9.3b)
breadboards: 1

parts:
  L1 = L6203 [chip_label=L6203 package="DIP (Dual Inline) [THT]"]
  C1 = Ceramic Capacitor [capacitance=220nF package="100 mil [THT, multilayer]"]
  M1 = DC Motor
  HER301 = Diode [package=diode-1n4001]
  HER301_2 = Diode [package=diode-1n4001]
  C2 = Ceramic Capacitor [capacitance=15nF package="100 mil [THT, multilayer]"]
  C3 = Ceramic Capacitor [capacitance=15nF package="100 mil [THT, multilayer]"]
  R1 = Resistor [tolerance=±5% resistance=10 package=THT]
  C4 = Ceramic Capacitor [capacitance=22nF package="100 mil [THT, multilayer]"]
  C5 = Ceramic Capacitor [capacitance=100nF package="100 mil [THT, multilayer]"]

nets:
  GND: L1.SENSE, L1.GND, C1.0, HER301.A, HER301_2.A, C5.0
  N1: L1.BOOT2, C2.0
  N2: L1.BOOT1, C3.0
  12V: L1.Vs, C5.1
  N3: L1.OUT2, M1.pin_1, HER301.C, C2.1, R1.Pin_0
  N4: L1.OUT1, M1.pin_2, HER301_2.C, C3.1, C4.0
  I/O pin: L1.IN1, L1.IN2
  N5: L1.Vref, C1.1
  PWM-pin: L1.ENABLE
  N6: R1.Pin_1, C4.1

custom parts:
  L6203: A DIP stand-in part for whatever IC you want. With 12 pins on a 300mil dual inline package (DIP) footprint.
