# Fritzing sketch driver_scheme (saved by Fritzing 0.9.3b)
breadboards: 1

parts:
  R2 = Resistor [tolerance=±5% resistance=10 package=THT]
  L2 = L6203 [chip_label=L6203 package="DIP (Dual Inline) [THT]"]
  C6 = Ceramic Capacitor [capacitance=15nF package="100 mil [THT, multilayer]"]
  C7 = Ceramic Capacitor [capacitance=15nF package="100 mil [THT, multilayer]"]
  C8 = Ceramic Capacitor [capacitance=100nF package="100 mil [THT, multilayer]"]
  C9 = Ceramic Capacitor [capacitance=22nF package="100 mil [THT, multilayer]"]
  C10 = Ceramic Capacitor [capacitance=220nF package="100 mil [THT, multilayer]"]
  M2 = DC Motor
  HER302 = Diode [package=diode-1n4001]
  HER303 = Diode [package=diode-1n4001]
  R3 = Resistor [tolerance=±5% resistance=10 package=THT]
  L3 = L6203 [chip_label=L6203 package="DIP (Dual Inline) [THT]"]
  C11 = Ceramic Capacitor [capacitance=15nF package="100 mil [THT, multilayer]"]
  C12 = Ceramic Capacitor [capacitance=15nF package="100 mil [THT, multilayer]"]
  C13 = Ceramic Capacitor [capacitance=100nF package="100 mil [THT, multilayer]"]
  C14 = Ceramic Capacitor [capacitance=22nF package="100 mil [THT, multilayer]"]
  C15 = Ceramic Capacitor [capacitance=220nF package="100 mil [THT, multilayer]"]
  M3 = DC Motor
  HER304 = Diode [package=diode-1n4001]
  HER305 = Diode [package=diode-1n4001]
  R4 = Resistor [tolerance=±5% resistance=10 package=THT]
  R5 = Resistor [tolerance=±5% resistance=10 package=THT]
  L4 = L6203 [chip_label=L6203 package="DIP (Dual Inline) [THT]"]
  C16 = Ceramic Capacitor [capacitance=15nF package="100 mil [THT, multilayer]"]
  C17 = Ceramic Capacitor [capacitance=15nF package="100 mil [THT, multilayer]"]
  C18 = Ceramic Capacitor [capacitance=100nF package="100 mil [THT, multilayer]"]
  C19 = Ceramic Capacitor [capacitance=22nF package="100 mil [THT, multilayer]"]
  C20 = Ceramic Capacitor [capacitance=220nF package="100 mil [THT, multilayer]"]
  L5 = L6203 [chip_label=L6203 package="DIP (Dual Inline) [THT]"]
  M4 = DC Motor
  HER306 = Diode [package=diode-1n4001]
  C21 = Ceramic Capacitor [capacitance=15nF package="100 mil [THT, multilayer]"]
  HER307 = Diode [package=diode-1n4001]
  C22 = Ceramic Capacitor [capacitance=100nF package="100 mil [THT, multilayer]"]
  C23 = Ceramic Capacitor [capacitance=15nF package="100 mil [THT, multilayer]"]
  C24 = Ceramic Capacitor [capacitance=22nF package="100 mil [THT, multilayer]"]
  C25 = Ceramic Capacitor [capacitance=220nF package="100 mil [THT, multilayer]"]
  M5 = DC Motor
  HER308 = Diode [package=diode-1n4001]
  HER309 = Diode [package=diode-1n4001]
  U1 = 74HC595 [package="DIP16 [THT]"]
  part = Resistor [tolerance=±5% resistance=220 package=THT]
  LED1 = LED - 5mm [color="Red (633nm)" package="5 mm [THT]"]
  LED2 = LED - 5mm [color="Red (633nm)" package="5 mm [THT]"]
  part_2 = Resistor [tolerance=±5% resistance=220 package=THT]
  part_3 = Resistor [tolerance=±5% resistance=220 package=THT]
  part_4 = Resistor [tolerance=±5% resistance=220 package=THT]
  LED3 = LED - 5mm [color="Red (633nm)" package="5 mm [THT]"]
  LED4 = LED - 5mm [color="Red (633nm)" package="5 mm [THT]"]
  part_5 = Resistor [tolerance=±5% resistance=220 package=THT]
  LED5 = LED - 5mm [color="Red (633nm)" package="5 mm [THT]"]
  part_6 = Resistor [tolerance=±5% resistance=220 package=THT]
  LED6 = LED - 5mm [color="Red (633nm)" package="5 mm [THT]"]
  part_7 = Resistor [tolerance=±5% resistance=220 package=THT]
  part_8 = Resistor [tolerance=±5% resistance=220 package=THT]
  LED7 = LED - 5mm [color="Red (633nm)" package="5 mm [THT]"]
  LED8 = LED - 5mm [color="Red (633nm)" package="5 mm [THT]"]

nets:
  N1: R2.Pin_0, L2.OUT2, C7.1, M2.pin_1, HER303.C
  N2: R2.Pin_1, C9.1
  GND: L2.SENSE, L2.GND, C8.0, C10.0, HER302.A, HER303.A, L3.SENSE, L3.GND, C13.0, C15.0, HER304.A, HER305.A, L4.SENSE, L4.GND, C18.0, C20.0, L5.SENSE, L5.GND, HER306.A, HER307.A, C22.0, C25.0, HER308.A, HER309.A, U1.GND, U1.OE, LED1.cathode, LED2.cathode, LED3.cathode, LED4.cathode, LED5.cathode, LED6.cathode, LED7.cathode, LED8.cathode
  N3: L2.BOOT2, C7.0
  N4: L2.BOOT1, C6.0
  12V: L2.Vs, C8.1, L3.Vs, C13.1, L4.Vs, C18.1, L5.Vs, C22.1
  N5: L2.OUT1, C6.1, C9.0, M2.pin_2, HER302.C
  N6: L2.IN1, U1.Q5, part.Pin_0
  N7: L2.IN2, U1.Q4, part_2.Pin_0
  N8: L2.Vref, C10.1
  PWM-pin: L2.ENABLE, L3.ENABLE, L4.ENABLE, L5.ENABLE
  N9: R3.Pin_0, L3.OUT2, C12.1, M3.pin_1, HER305.C
  N10: R3.Pin_1, C14.1
  N11: L3.BOOT2, C12.0
  N12: L3.BOOT1, C11.0
  N13: L3.OUT1, C11.1, C14.0, M3.pin_2, HER304.C
  N14: L3.IN1, U1.Q3, part_5.Pin_0
  N15: L3.IN2, U1.Q2, part_6.Pin_0
  N16: L3.Vref, C15.1
  N17: R4.Pin_0, L5.OUT2, C23.1, M5.pin_1, HER309.C
  N18: R4.Pin_1, C24.1
  N19: R5.Pin_0, L4.OUT2, C17.1, M4.pin_1, HER307.C
  N20: R5.Pin_1, C19.1
  N21: L4.BOOT2, C17.0
  N22: L4.BOOT1, C16.0
  N23: L4.OUT1, C16.1, C19.0, M4.pin_2, HER306.C
  N24: L4.IN1, U1.Q7, part_4.Pin_0
  N25: L4.IN2, U1.Q6, part_3.Pin_0
  N26: L4.Vref, C20.1
  N27: L5.BOOT2, C23.0
  N28: L5.BOOT1, C21.0
  N29: L5.OUT1, C21.1, C24.0, M5.pin_2, HER308.C
  N30: L5.IN1, U1.Q1, part_7.Pin_0
  N31: L5.IN2, U1.Q0, part_8.Pin_0
  N32: L5.Vref, C25.1
  5V: U1.MR, U1.VCC
  clockPin: U1.SH_CP
  latchPin: U1.ST_CP
  dataPin: U1.DS
  N33: part.Pin_1, LED1.anode
  N34: LED2.anode, part_2.Pin_1
  N35: part_3.Pin_1, LED3.anode
  N36: part_4.Pin_1, LED4.anode
  N37: part_5.Pin_1, LED5.anode
  N38: part_6.Pin_1, LED6.anode
  N39: part_7.Pin_1, LED7.anode
  N40: part_8.Pin_1, LED8.anode

custom parts:
  L6203: A DIP stand-in part for whatever IC you want. With 12 pins on a 300mil dual inline package (DIP) footprint.
