# Fritzing sketch kicker_scheme (saved by Fritzing 0.9.3b)
breadboards: 1

parts:
  U1 = Optocoupler [package=THT]
  R1 = Resistor [tolerance=±5% resistance=1k package=THT]
  Q1 = Basic FET N-Channel [package="TO220 [THT]"]
  C1 = Electrolytic Capacitor [capacitance=1µF package="100 mil [THT, electrolytic]"]
  U2 = Optocoupler [package=THT]
  R2 = Resistor [tolerance=±5% resistance=1k package=THT]
  R3 = Resistor [tolerance=±5% resistance=1k package=THT]
  L1 = Solenoid
  Q2 = Basic FET N-Channel [package="TO220 [THT]"]
  D1 = Rectifier Diode [part_number=1N4001 package="300 mil [THT]"]
  R4 = Resistor [tolerance=±5% resistance=1k package=THT]
  C2 = Ceramic Capacitor [capacitance=100nF package="100 mil [THT, multilayer]"]

nets:
  N1: U1.Pin_1, R1.Pin_0
  GND: U1.Pin_2, U1.Pin_4, C1.-, U2.Pin_2, Q2.source, R4.Pin_0, C2.0
  N2: U1.Pin_5, Q1.gate, R3.Pin_0
  net label: R1.Pin_1, R2.Pin_1, C2.1
  24V: Q1.drain, U2.Pin_5, R3.Pin_1
  N3: Q1.source, C1.+, D1.anode
  N4: U2.Pin_1, R2.Pin_0
  N5: U2.Pin_4, Q2.gate, R4.Pin_1
  N6: L1.pin1, D1.cathode
  N7: L1.pin2, Q2.drain
