# Fritzing sketch hub_scheme (saved by Fritzing 0.9.3b)
breadboards: 1

parts:
  IC2 = DIP - 16 pins [chip_label="Multiplexor 4x2" package="DIP (Dual Inline) [THT]"]
  IC4 = DIP - 8 pins [chip_label="light sensor" package="DIP (Dual Inline) [THT]"]
  IC5 = DIP - 8 pins [chip_label="light sensor" package="DIP (Dual Inline) [THT]"]
  IC6 = DIP - 8 pins [chip_label="light sensor" package="DIP (Dual Inline) [THT]"]
  IC7 = DIP - 8 pins [chip_label="light sensor" package="DIP (Dual Inline) [THT]"]
  Q1 = PNP-Transistor [package="TO92 [THT]"]
  Q2 = PNP-Transistor [package="TO92 [THT]"]
  Q3 = PNP-Transistor [package="TO92 [THT]"]
  Q4 = PNP-Transistor [package="TO92 [THT]"]
  S1 = Pushbutton [package=THT]
  S2 = Pushbutton [package=THT]
  S3 = Pushbutton [package=THT]
  S4 = Pushbutton [package=THT]

nets:
  I/O pin: IC2.A0, IC2.A1, IC4.A0, IC4.A1, IC4.A2, IC5.A0, IC5.A1, IC5.A2, IC6.A0, IC6.A1, IC7.A0, IC7.A1
  Out: IC2.Zb
  GND: IC2.E, IC2.Vss, IC2.Vee, IC4.gnd, IC5.gnd, IC6.gnd, IC7.gnd
  N1: IC2.Yb0, IC7.Out
  N2: IC2.Yb1, IC6.Out
  N3: IC2.Yb2, IC4.Out
  N4: IC2.Yb3, IC5.Out
  5V: IC2.Vdd, IC4.5V, IC5.5V, IC6.5V, IC7.5V, S1.leg0, S2.leg0, S3.leg0, S4.leg0
  N5: IC4.12V, Q2.C
  N6: IC5.12V, Q1.C
  N7: IC6.A2, IC7.A2
  N8: IC6.12V, Q3.C
  N9: IC7.12V, Q4.C
  12V: Q1.E, Q2.E, Q3.E, Q4.E
  N10: Q1.B, S1.leg1
  N11: Q2.B, S2.leg1
  N12: Q3.B, S3.leg1
  N13: Q4.B, S4.leg1

custom parts:
  DIP - 16 pins: A DIP stand-in part for whatever IC you want. With 16 pins on a 300mil dual inline package (DIP) footprint.
  DIP - 8 pins: A DIP stand-in part for whatever IC you want. With 8 pins on a 300mil dual inline package (DIP) footprint.
