# Fritzing sketch light_sensor_scheme (saved by Fritzing 0.9.3b)
breadboards: 1

parts:
  R1 = Photocell (LDR) [package=THT]
  3V_20mA = Super Flux LED blue [color=White]
  R3 = Resistor [tolerance=±5% resistance=100 package=THT]
  3V_20mA_2 = Super Flux LED blue [color=White]
  3V_20mA_3 = Super Flux LED blue [color=White]
  3V_20mA_4 = Super Flux LED blue [color=White]
  3V_20mA_5 = Super Flux LED blue [color=White]
  3V_20mA_6 = Super Flux LED blue [color=White]
  3V_20mA_7 = Super Flux LED blue [color=White]
  3V_20mA_8 = Super Flux LED blue [color=White]
  R4 = Resistor [tolerance=±5% resistance=100 package=THT]
  R5 = Trimmer Potentiometer [maximum_resistance=1kΩ package=THT]
  R13 = Resistor [tolerance=±5% resistance=1k package=THT]
  R14 = Photocell (LDR) [package=THT]
  R15 = Resistor [tolerance=±5% resistance=1k package=THT]
  R16 = Photocell (LDR) [package=THT]
  R17 = Resistor [tolerance=±5% resistance=1k package=THT]
  R18 = Photocell (LDR) [package=THT]
  R19 = Resistor [tolerance=±5% resistance=1k package=THT]
  R20 = Photocell (LDR) [package=THT]
  R21 = Resistor [tolerance=±5% resistance=1k package=THT]
  R22 = Photocell (LDR) [package=THT]
  R23 = Resistor [tolerance=±5% resistance=1k package=THT]
  R24 = Photocell (LDR) [package=THT]
  R25 = Resistor [tolerance=±5% resistance=1k package=THT]
  R26 = Photocell (LDR) [package=THT]
  R27 = Resistor [tolerance=±5% resistance=1k package=THT]
  U1 = SN74HC251 [package=so016]
  C1 = Ceramic Capacitor [capacitance=10µF package="100 mil [THT, multilayer]"]

nets:
  5V: R1.pin_0, R14.pin_0, R16.pin_0, R18.pin_0, R20.pin_0, R22.pin_0, R24.pin_0, R26.pin_0, U1.VCC
  N1: R1.pin_1, R13.Pin_0, U1.D0
  N2: 3V_20mA.cathode, 3V_20mA_2.anode
  N3: 3V_20mA.anode, R3.Pin_1
  N4: R3.Pin_0, R4.Pin_0, R5.wiper
  N5: 3V_20mA_2.cathode, 3V_20mA_3.anode
  N6: 3V_20mA_3.cathode, 3V_20mA_4.anode
  GND: 3V_20mA_4.cathode, 3V_20mA_8.cathode, R5.leg1, R13.Pin_1, R15.Pin_1, R17.Pin_1, R19.Pin_1, R21.Pin_1, R23.Pin_1, R25.Pin_1, R27.Pin_1, U1.OE, U1.GND, C1.0
  N7: 3V_20mA_5.cathode, 3V_20mA_6.anode
  N8: 3V_20mA_5.anode, R4.Pin_1
  N9: 3V_20mA_6.cathode, 3V_20mA_7.anode
  N10: 3V_20mA_7.cathode, 3V_20mA_8.anode
  12V: R5.leg2, C1.1
  N11: R14.pin_1, R15.Pin_0, U1.D1
  N12: R16.pin_1, R17.Pin_0, U1.D2
  N13: R18.pin_1, R19.Pin_0, U1.D3
  N14: R20.pin_1, R21.Pin_0, U1.D4
  N15: R22.pin_1, R23.Pin_0, U1.D5
  N16: R24.pin_1, R25.Pin_0, U1.D6
  N17: R26.pin_1, R27.Pin_0, U1.D7
  analog pin: U1.W
  I/O pin: U1.C, U1.B, U1.A
